# Fritzing sketch LukeShaw_Diagram (saved by Fritzing 1.0.7)
breadboards: 1

parts:
  L298N1 = L298N DC motor driver
  M1 = DC Motor [voltage_(max)=6V voltage_(min)=3V]
  M2 = DC Motor [voltage_(max)=6V voltage_(min)=3V]
  A1 = ESP32-C6-DevKitC-1
  BAT1 = Lithium Ion Polymer Battery 11.1v 5000mah
  J1 = Basic Servo
  BATT1 = 3xAAA Switchable Battery Pack w/Bare Wire
  3-pins_Hall_Effect_Sensor1 = mystery part, 3 pins [chip_label="Hall Effect Sensor"]
  3-pins_Hall_Effect_Sensor2 = mystery part, 3 pins [chip_label="Hall Effect Sensor"]

nets:
  N1: L298N1.OUT1, M2.pin_2
  N2: L298N1.OUT2, M2.pin_1
  N3: L298N1.OUT3, M1.pin_2
  N4: L298N1.OUT4, M1.pin_1
  N5: L298N1.12V, BAT1.positive
  N6: L298N1.GND, A1.Pin_17, BAT1.negative, 3-pins_Hall_Effect_Sensor1.pin3, 3-pins_Hall_Effect_Sensor2.pin3
  N7: L298N1.5V, A1.Pin_15, A1.Pin_32, 3-pins_Hall_Effect_Sensor1.pin2, 3-pins_Hall_Effect_Sensor2.pin2
  N8: L298N1.ENA, A1.Pin_7
  N9: L298N1.ENB, A1.Pin_22
  N10: L298N1.IN1, A1.Pin_5
  N11: L298N1.IN2, A1.Pin_6
  N12: L298N1.IN3, A1.Pin_10
  N13: L298N1.IN4, A1.Pin_21
  N14: A1.Pin_11, 3-pins_Hall_Effect_Sensor1.pin1
  N15: A1.Pin_12, 3-pins_Hall_Effect_Sensor2.pin1
  N16: J1.gnd, BATT1.NEG
  N17: J1.vcc, BATT1.POS

notes:
  Left Motor
  Right Motor
  L298N Motor Driver Board

custom parts:
  L298N DC motor driver: 2x DC motor driver with 78M05 positive voltage regulator (7..35 V) L298N: max 46 V, 2 A Set 5 V Enable jumper to enable 5 V regultor (needed for the L298N) and +5 V output at screw terminal or supply external +5 V at screw terminal Set ENA and/or ENB to +5 V to enable motor permanently or supply ENA and/or ENB with PWM signal IN1 and IN2 set rotation directory for motor A (OUT1/OUT2) IN2 and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
  ESP32-C6-DevKitC-1: ESP32-C6-DevKitC-1 is an entry-level development board based on ESP32-C6-WROOM-1(U), a general-purpose module with a 8 MB SPI flash. This board integrates complete Wi-Fi, Bluetooth LE, Zigbee, and Thread functions.
  3xAAA Switchable Battery Pack w/Bare Wire: 3xAAA Switchable Battery Pack w/Bare Wire Connectors
